// Logisim project ex1.circ as structural Verilog: 1 circuit, main circuit generate_immediate
module generate_immediate (
  input  [31:0] INSTRUCTION,
  output [31:0] IMMEDIATE
);

  Multiplexer #(.enable("false"), .width(21)) multiplexer_1 (
    .in0({21{1'b0}}), .in1({21{1'b1}}), .out(IMMEDIATE[31:11]), .sel(INSTRUCTION[31]));

  assign IMMEDIATE[10:0] = {INSTRUCTION[30:25], INSTRUCTION[11:7]};
endmodule
