// Logisim project ex2.circ as structural Verilog: 1 circuit, main circuit compute_BrUn
module compute_BrUn (
  input  [31:0] INSTRUCTION,
  output BrUn
);

  wire comparator_1_gt;

  Multiplexer #(.enable("false")) multiplexer_1 (.in0(1'b1), .in1(1'b0), .out(BrUn), .sel(comparator_1_gt));
  Comparator #(.mode("unsigned"), .width(3)) comparator_1 (
    .a(3'b110), .b(INSTRUCTION[14:12]), .gt(comparator_1_gt));  // open: eq, lt
endmodule
