// Logisim project control-logic.circ as structural Verilog: 1 circuit, main circuit control_logic
module control_logic (
  input  [31:0] Instruction,
  input  BrEq,
  input  BrLt,
  output PCSel,
  output RegWEn,
  output [2:0] ImmSel,
  output BrUn,
  output ASel,
  output BSel,
  output [3:0] ALUSel,
  output MemWEn,
  output [1:0] WBSel
);

  wire add, addi, and_28_out, and_29_out, and_30_out, and_31_out, andi, auipc, B, beq, bge, bgeu, blt, bltu,
       bne, comparator_1_eq, comparator_2_eq, comparator_3_eq, comparator_4_eq, comparator_5_eq,
       comparator_6_eq, comparator_7_eq, comparator_8_eq, comparator_9_eq, comparator_11_eq,
       comparator_12_eq, comparator_13_eq, comparator_14_eq, comparator_15_eq, comparator_16_eq,
       comparator_17_eq, comparator_18_eq, comparator_19_eq, comparator_20_eq, comparator_22_eq,
       comparator_23_eq, comparator_24_eq, comparator_25_eq, comparator_26_eq, comparator_27_eq,
       comparator_28_eq, comparator_29_eq, comparator_30_eq, comparator_31_eq, comparator_32_eq,
       comparator_33_eq, comparator_34_eq, comparator_35_eq, comparator_36_eq, comparator_37_eq,
       comparator_38_eq, comparator_39_eq, comparator_40_eq, comparator_41_eq, comparator_43_eq,
       comparator_44_eq, comparator_45_eq, comparator_46_eq, comparator_47_eq, comparator_48_eq,
       comparator_52_eq, comparator_53_eq, I, is_and, is_or, is_sll, is_slt, is_sra, is_srl, is_xor, jal,
       jalr, JU, L, lb, lh, lui, lw, mul, mulh, mulhu, not_1_out, not_2_out, or_1_out, or_2_out, ori, R, S,
       sb, sh, slli, slti, srai, srli, srli_srai, sub, sw, xori;
  wire [1:0] priority_encoder_5_out, priority_encoder_6_out, priority_encoder_7_out;
  wire [2:0] Kind, priority_encoder_1_out, priority_encoder_4_out;
  wire [3:0] R_Input;
  wire [5:0] B_Input, I_Input, JU_Input, L_Input, ROMInput, S_Input;
  wire [15:14] rom_1_data;

  Comparator #(.mode("unsigned"), .width(3)) comparator_1 (
    .a(3'b000), .b(Instruction[14:12]), .eq(comparator_1_eq));  // open: gt, lt
  Comparator #(.mode("unsigned"), .width(3)) comparator_2 (
    .a(3'b111), .b(Instruction[14:12]), .eq(comparator_2_eq));  // open: gt, lt
  Comparator #(.mode("unsigned"), .width(3)) comparator_3 (
    .a(3'b110), .b(Instruction[14:12]), .eq(comparator_3_eq));  // open: gt, lt
  Comparator #(.mode("unsigned"), .width(3)) comparator_4 (
    .a(3'b100), .b(Instruction[14:12]), .eq(comparator_4_eq));  // open: gt, lt
  Comparator #(.mode("unsigned"), .width(3)) comparator_5 (
    .a(3'b001), .b(Instruction[14:12]), .eq(comparator_5_eq));  // open: gt, lt
  Comparator #(.mode("unsigned"), .width(3)) comparator_6 (
    .a(3'b101), .b(Instruction[14:12]), .eq(comparator_6_eq));  // open: gt, lt
  Comparator #(.mode("unsigned"), .width(7)) comparator_7 (
    .a({7{1'b0}}), .b(Instruction[31:25]), .eq(comparator_7_eq));  // open: gt, lt
  Comparator #(.mode("unsigned"), .width(7)) comparator_8 (
    .a(7'b0100000), .b(Instruction[31:25]), .eq(comparator_8_eq));  // open: gt, lt
  Comparator #(.mode("unsigned"), .width(3)) comparator_9 (
    .a(3'b010), .b(Instruction[14:12]), .eq(comparator_9_eq));  // open: gt, lt
  ROM #(.addrWidth(6), .dataWidth(16)) rom_1 (
    .addr(ROMInput), .data({rom_1_data, WBSel, MemWEn, ALUSel, BSel, ASel, BrUn, ImmSel, RegWEn}));
  Comparator #(.mode("unsigned"), .width(7)) comparator_10 (
    .a(7'b0010011), .b(Instruction[6:0]), .eq(I));  // open: gt, lt
  and and_1 (addi, comparator_1_eq, I);
  and and_2 (andi, comparator_2_eq, I);
  and and_3 (ori, comparator_3_eq, I);
  and and_4 (xori, comparator_4_eq, I);
  and and_5 (slli, comparator_5_eq, I);
  and and_6 (srli_srai, comparator_6_eq, I);
  and and_7 (srli, comparator_7_eq, srli_srai);
  and and_8 (srai, comparator_8_eq, srli_srai);
  and and_9 (slti, comparator_9_eq, I);
  Priority_Encoder priority_encoder_1 (
    .in0(addi), .in1(slli), .in2(slti), .in3(xori), .in4(srli), .in5(srai), .in6(ori), .in7(andi),
    .out(priority_encoder_1_out), .en_in(I));  // open: gs, en_out
  Adder #(.width(6)) adder_1 (.a({3'b000, priority_encoder_1_out}), .b(6'b001111), .out(I_Input));  // open: cin, cout
  Comparator #(.mode("unsigned"), .width(3)) comparator_11 (
    .a(3'b000), .b(Instruction[14:12]), .eq(comparator_11_eq));  // open: gt, lt
  Comparator #(.mode("unsigned"), .width(7)) comparator_12 (
    .a({7{1'b0}}), .b(Instruction[31:25]), .eq(comparator_12_eq));  // open: gt, lt
  Comparator #(.mode("unsigned"), .width(3)) comparator_13 (
    .a(3'b000), .b(Instruction[14:12]), .eq(comparator_13_eq));  // open: gt, lt
  Comparator #(.mode("unsigned"), .width(7)) comparator_14 (
    .a(7'b0100000), .b(Instruction[31:25]), .eq(comparator_14_eq));  // open: gt, lt
  Comparator #(.mode("unsigned"), .width(3)) comparator_15 (
    .a(3'b111), .b(Instruction[14:12]), .eq(comparator_15_eq));  // open: gt, lt
  Comparator #(.mode("unsigned"), .width(7)) comparator_16 (
    .a({7{1'b0}}), .b(Instruction[31:25]), .eq(comparator_16_eq));  // open: gt, lt
  Comparator #(.mode("unsigned"), .width(3)) comparator_17 (
    .a(3'b110), .b(Instruction[14:12]), .eq(comparator_17_eq));  // open: gt, lt
  Comparator #(.mode("unsigned"), .width(7)) comparator_18 (
    .a({7{1'b0}}), .b(Instruction[31:25]), .eq(comparator_18_eq));  // open: gt, lt
  Comparator #(.mode("unsigned"), .width(3)) comparator_19 (
    .a(3'b100), .b(Instruction[14:12]), .eq(comparator_19_eq));  // open: gt, lt
  Comparator #(.mode("unsigned"), .width(7)) comparator_20 (
    .a({7{1'b0}}), .b(Instruction[31:25]), .eq(comparator_20_eq));  // open: gt, lt
  Comparator #(.mode("unsigned"), .width(7)) comparator_21 (
    .a(7'b0110011), .b(Instruction[6:0]), .eq(R));  // open: gt, lt
  and and_10 (add, comparator_11_eq, comparator_12_eq, R);
  and and_11 (sub, comparator_13_eq, comparator_14_eq, R);
  and and_12 (is_and, comparator_15_eq, comparator_16_eq, R);
  and and_13 (is_or, comparator_17_eq, comparator_18_eq, R);
  and and_14 (is_xor, comparator_19_eq, comparator_20_eq, R);
  Priority_Encoder priority_encoder_2 (
    .in0(R), .in1(I), .in2(L), .in3(B), .in4(S), .in5(JU), .out(Kind));  // open: in6, in7, en_in, gs, en_out
  Comparator #(.mode("unsigned"), .width(3)) comparator_22 (
    .a(3'b001), .b(Instruction[14:12]), .eq(comparator_22_eq));  // open: gt, lt
  Comparator #(.mode("unsigned"), .width(7)) comparator_23 (
    .a({7{1'b0}}), .b(Instruction[31:25]), .eq(comparator_23_eq));  // open: gt, lt
  Comparator #(.mode("unsigned"), .width(3)) comparator_24 (
    .a(3'b101), .b(Instruction[14:12]), .eq(comparator_24_eq));  // open: gt, lt
  Comparator #(.mode("unsigned"), .width(7)) comparator_25 (
    .a({7{1'b0}}), .b(Instruction[31:25]), .eq(comparator_25_eq));  // open: gt, lt
  Comparator #(.mode("unsigned"), .width(3)) comparator_26 (
    .a(3'b101), .b(Instruction[14:12]), .eq(comparator_26_eq));  // open: gt, lt
  Comparator #(.mode("unsigned"), .width(7)) comparator_27 (
    .a(7'b0100000), .b(Instruction[31:25]), .eq(comparator_27_eq));  // open: gt, lt
  Comparator #(.mode("unsigned"), .width(3)) comparator_28 (
    .a(3'b010), .b(Instruction[14:12]), .eq(comparator_28_eq));  // open: gt, lt
  Comparator #(.mode("unsigned"), .width(7)) comparator_29 (
    .a({7{1'b0}}), .b(Instruction[31:25]), .eq(comparator_29_eq));  // open: gt, lt
  Comparator #(.mode("unsigned"), .width(3)) comparator_30 (
    .a(3'b000), .b(Instruction[14:12]), .eq(comparator_30_eq));  // open: gt, lt
  Comparator #(.mode("unsigned"), .width(7)) comparator_31 (
    .a(7'b0000001), .b(Instruction[31:25]), .eq(comparator_31_eq));  // open: gt, lt
  and and_15 (is_sll, comparator_22_eq, comparator_23_eq, R);
  and and_16 (is_srl, comparator_24_eq, comparator_25_eq, R);
  and and_17 (is_sra, comparator_26_eq, comparator_27_eq, R);
  and and_18 (is_slt, comparator_28_eq, comparator_29_eq, R);
  and and_19 (mul, comparator_30_eq, comparator_31_eq, R);
  Multiplexer #(.enable("false"), .select(3), .width(6)) multiplexer_1 (
    .in0({2'b00, R_Input}), .in1(I_Input), .in2(L_Input), .in3(B_Input), .in4(S_Input), .in5(JU_Input),
    .out(ROMInput), .sel(Kind));  // open: in6, in7
  Comparator #(.mode("unsigned"), .width(3)) comparator_32 (
    .a(3'b001), .b(Instruction[14:12]), .eq(comparator_32_eq));  // open: gt, lt
  Comparator #(.mode("unsigned"), .width(7)) comparator_33 (
    .a(7'b0000001), .b(Instruction[31:25]), .eq(comparator_33_eq));  // open: gt, lt
  Comparator #(.mode("unsigned"), .width(3)) comparator_34 (
    .a(3'b011), .b(Instruction[14:12]), .eq(comparator_34_eq));  // open: gt, lt
  Comparator #(.mode("unsigned"), .width(7)) comparator_35 (
    .a(7'b0000001), .b(Instruction[31:25]), .eq(comparator_35_eq));  // open: gt, lt
  and and_20 (mulh, comparator_32_eq, comparator_33_eq, R);
  and and_21 (mulhu, comparator_34_eq, comparator_35_eq, R);
  Priority_Encoder #(.select(4)) priority_encoder_3 (
    .in0(add), .in1(mul), .in2(sub), .in3(is_sll), .in4(mulh), .in5(mulhu), .in6(is_slt), .in7(is_xor),
    .in8(is_srl), .in9(is_sra), .in10(is_or), .in11(is_and), .out(R_Input), .en_in(R));  // open: in12, in13, in14, in15, gs, en_out
  Comparator #(.mode("unsigned"), .width(3)) comparator_36 (
    .a(3'b000), .b(Instruction[14:12]), .eq(comparator_36_eq));  // open: gt, lt
  Comparator #(.mode("unsigned"), .width(3)) comparator_37 (
    .a(3'b101), .b(Instruction[14:12]), .eq(comparator_37_eq));  // open: gt, lt
  Comparator #(.mode("unsigned"), .width(3)) comparator_38 (
    .a(3'b111), .b(Instruction[14:12]), .eq(comparator_38_eq));  // open: gt, lt
  Comparator #(.mode("unsigned"), .width(3)) comparator_39 (
    .a(3'b100), .b(Instruction[14:12]), .eq(comparator_39_eq));  // open: gt, lt
  Comparator #(.mode("unsigned"), .width(3)) comparator_40 (
    .a(3'b110), .b(Instruction[14:12]), .eq(comparator_40_eq));  // open: gt, lt
  Comparator #(.mode("unsigned"), .width(3)) comparator_41 (
    .a(3'b001), .b(Instruction[14:12]), .eq(comparator_41_eq));  // open: gt, lt
  Comparator #(.mode("unsigned"), .width(7)) comparator_42 (
    .a(7'b1100011), .b(Instruction[6:0]), .eq(B));  // open: gt, lt
  and and_22 (beq, comparator_36_eq, B);
  and and_23 (bge, comparator_37_eq, B);
  and and_24 (bgeu, comparator_38_eq, B);
  and and_25 (blt, comparator_39_eq, B);
  and and_26 (bltu, comparator_40_eq, B);
  and and_27 (bne, comparator_41_eq, B);
  not not_1 (not_1_out, BrLt);
  not not_2 (not_2_out, BrEq);
  Priority_Encoder priority_encoder_4 (
    .in0(beq), .in1(bne), .in2(blt), .in3(bge), .in4(bltu), .in5(bgeu), .out(priority_encoder_4_out),
    .en_in(B));  // open: in6, in7, gs, en_out
  and and_28 (and_28_out, BrEq, beq);
  or or_1 (or_1_out, bgeu, bge);
  or or_2 (or_2_out, blt, bltu);
  Adder #(.width(6)) adder_2 (.a({3'b000, priority_encoder_4_out}), .b(6'b011010), .out(B_Input));  // open: cin, cout
  and and_29 (and_29_out, or_1_out, not_1_out);
  and and_30 (and_30_out, or_2_out, BrLt);
  and and_31 (and_31_out, bne, not_2_out);
  or or_3 (PCSel, and_28_out, and_29_out, and_30_out, and_31_out, jal, jalr);
  Comparator #(.mode("unsigned"), .width(3)) comparator_43 (
    .a(3'b000), .b(Instruction[14:12]), .eq(comparator_43_eq));  // open: gt, lt
  Comparator #(.mode("unsigned"), .width(3)) comparator_44 (
    .a(3'b001), .b(Instruction[14:12]), .eq(comparator_44_eq));  // open: gt, lt
  Comparator #(.mode("unsigned"), .width(3)) comparator_45 (
    .a(3'b010), .b(Instruction[14:12]), .eq(comparator_45_eq));  // open: gt, lt
  Comparator #(.mode("unsigned"), .width(3)) comparator_46 (
    .a(3'b000), .b(Instruction[14:12]), .eq(comparator_46_eq));  // open: gt, lt
  Comparator #(.mode("unsigned"), .width(3)) comparator_47 (
    .a(3'b001), .b(Instruction[14:12]), .eq(comparator_47_eq));  // open: gt, lt
  Comparator #(.mode("unsigned"), .width(3)) comparator_48 (
    .a(3'b010), .b(Instruction[14:12]), .eq(comparator_48_eq));  // open: gt, lt
  Comparator #(.mode("unsigned"), .width(7)) comparator_49 (
    .a(7'b0000011), .b(Instruction[6:0]), .eq(L));  // open: gt, lt
  Comparator #(.mode("unsigned"), .width(7)) comparator_50 (
    .a(7'b0100011), .b(Instruction[6:0]), .eq(S));  // open: gt, lt
  and and_32 (lb, comparator_43_eq, L);
  and and_33 (lh, comparator_44_eq, L);
  and and_34 (lw, comparator_45_eq, L);
  and and_35 (sb, comparator_46_eq, S);
  and and_36 (sh, comparator_47_eq, S);
  and and_37 (sw, comparator_48_eq, S);
  Priority_Encoder #(.select(2)) priority_encoder_5 (
    .in0(lb), .in1(lh), .in2(lw), .out(priority_encoder_5_out), .en_in(L));  // open: in3, gs, en_out
  Priority_Encoder #(.select(2)) priority_encoder_6 (
    .in0(sb), .in1(sh), .in2(sw), .out(priority_encoder_6_out), .en_in(S));  // open: in3, gs, en_out
  Adder #(.width(6)) adder_3 (.a({4'b0000, priority_encoder_5_out}), .b(6'b001100), .out(L_Input));  // open: cin, cout
  Adder #(.width(6)) adder_4 (.a({4'b0000, priority_encoder_6_out}), .b(6'b010111), .out(S_Input));  // open: cin, cout
  Comparator #(.mode("unsigned"), .width(7)) comparator_51 (
    .a(7'b1101111), .b(Instruction[6:0]), .eq(jal));  // open: gt, lt
  Comparator #(.mode("unsigned"), .width(7)) comparator_52 (
    .a(7'b1100111), .b(Instruction[6:0]), .eq(comparator_52_eq));  // open: gt, lt
  Comparator #(.mode("unsigned"), .width(3)) comparator_53 (
    .a(3'b000), .b(Instruction[14:12]), .eq(comparator_53_eq));  // open: gt, lt
  Comparator #(.mode("unsigned"), .width(7)) comparator_54 (
    .a(7'b0010111), .b(Instruction[6:0]), .eq(auipc));  // open: gt, lt
  Comparator #(.mode("unsigned"), .width(7)) comparator_55 (
    .a(7'b0110111), .b(Instruction[6:0]), .eq(lui));  // open: gt, lt
  or or_4 (JU, auipc, lui, jal, jalr);
  and and_38 (jalr, comparator_52_eq, comparator_53_eq);
  Priority_Encoder #(.select(2)) priority_encoder_7 (
    .in0(auipc), .in1(lui), .in2(jal), .in3(jalr), .out(priority_encoder_7_out), .en_in(JU));  // open: gs, en_out
  Adder #(.width(6)) adder_5 (.a({4'b0000, priority_encoder_7_out}), .b(6'b100000), .out(JU_Input));  // open: cin, cout

  // Other names for the same wires on the sheet: opcode[6:0] = Instruction[6:0]; funct3[2:0] = Instruction[14:12];
  //   funct7[6:0] = Instruction[31:25]

  // Notes on the sheet:
  //   INPUTS to your circuit
  //   Connect ROM Input here ->
  //   contents of rom_1 (hex, n*v repeats v):
  //   100f 140f 160f 108f 148f 158f 110f 120f 128f 168f 130f 138f 41 41 41 1041 10c1 1141 1241 12c1 16c1
  //   1341 13c1 1842 1842 1842 4*1064 1074 1074 1067 3547 2069 2041
  //   ROM FOR CONTROL LOGIC
  //   DON'T CHANGE THE LOCATIONS OF THE INPUTS AND OUTPUTS!
  //   This is only if you choose to do the ROM option
  //   CONNECT
  //   WIRE
  //   TO
  //   USE
  //   ROM
  //   OUTPUT from your circuit
  //   Reminder: If using ROM, use combinational logic for PCSel
endmodule
