// Logisim project cpu.circ as structural Verilog: 1 circuit, main circuit cpu
module cpu (
  input  clk,
  input  [31:0] Instruction,
  input  [31:0] MemReadData,
  output [31:0] MemAddress,
  output [31:0] ProgramCounter,
  output [31:0] ra,
  output [31:0] sp,
  output [31:0] t0,
  output [31:0] t1,
  output [31:0] t2,
  output [31:0] s0,
  output [31:0] s1,
  output [31:0] a0,
  output [3:0] MemWriteMask,
  output [31:0] MemWriteData
);

  wire ASel, BrEq, BrLt, BrUn, BSel, L, lb, lh, lw, MemWEn, PCSel, RegWEn;
  wire [1:0] priority_encoder_1_out, WBSel;
  wire [2:0] funct3, ImmSel;
  wire [3:0] ALUSel;
  wire [5:0] L_Input;
  wire [6:0] funct7;
  wire [24:0] nextInstruction;
  wire [31:0] adder_1_out, adder_2_out, DtoR, Imme, multiplexer_1_out, multiplexer_2_out, multiplexer_3_out,
       multiplexer_4_out, multiplexer_5_out, nextProgramCounter, RRD1, RRD2;

  Adder #(.width(32)) adder_1 (.a(ProgramCounter), .b(32'h4), .out(adder_1_out));  // open: cin, cout
  Multiplexer #(.enable("false"), .width(32)) multiplexer_1 (
    .in0(RRD1), .in1(nextProgramCounter), .out(multiplexer_1_out), .sel(ASel));
  Multiplexer #(.enable("false"), .width(32)) multiplexer_2 (
    .in0(RRD2), .in1(Imme), .out(multiplexer_2_out), .sel(BSel));
  Multiplexer #(.enable("false"), .width(32)) multiplexer_3 (
    .in0(adder_1_out), .in1(MemAddress), .out(multiplexer_3_out), .sel(PCSel));
  Multiplexer #(.enable("false"), .width(32)) multiplexer_4 (
    .in0(Instruction), .in1(32'h13), .out(multiplexer_4_out), .sel(PCSel));
  Adder #(.width(32)) adder_2 (.a(nextProgramCounter), .b(32'h4), .out(adder_2_out));  // open: cin, cout
  alu alu_1 (.ALUResult(MemAddress), .A(multiplexer_1_out), .B(multiplexer_2_out), .ALUSel(ALUSel));
  control_logic control_logic_1 (
    .PCSel(PCSel), .RegWEn(RegWEn), .ImmSel(ImmSel), .BrUn(BrUn), .ASel(ASel), .BSel(BSel), .ALUSel(ALUSel),
    .MemWEn(MemWEn), .WBSel(WBSel),
    .Instruction({funct7, nextInstruction[24:15], funct3, nextInstruction[11:0]}), .BrEq(BrEq), .BrLt(BrLt));
  Register #(.width(32)) PC (.D(multiplexer_3_out), .clk(clk), .Q(ProgramCounter));  // open: en, clr
  Register #(.width(32)) register_1 (
    .D(multiplexer_4_out), .clk(clk), .Q({funct7, nextInstruction[24:15], funct3, nextInstruction[11:0]}));  // open: en, clr
  Multiplexer #(.enable("false"), .select(2), .width(32)) multiplexer_5 (
    .in0(DtoR), .in1(MemAddress), .in2(adder_2_out), .in3(Imme), .out(multiplexer_5_out), .sel(WBSel));
  Register #(.width(32)) register_2 (.D(ProgramCounter), .clk(clk), .Q(nextProgramCounter));  // open: en, clr
  regfile regfile_1 (
    .ReadReg1(nextInstruction[19:15]), .ReadReg2(nextInstruction[24:20]), .WriteReg(nextInstruction[11:7]),
    .RegWriteData(multiplexer_5_out), .RegWEn(RegWEn), .clk(clk), .ra(ra), .sp(sp), .t0(t0), .t1(t1),
    .t2(t2), .s0(s0), .s1(s1), .a0(a0), .RegReadData1(RRD1), .RegReadData2(RRD2));
  partial_store partial_store_1 (
    .Instruction({funct7, nextInstruction[24:15], funct3, nextInstruction[11:0]}), .MemAddress(MemAddress),
    .DataFromReg(RRD2), .MemWEn(MemWEn), .MemWriteMask(MemWriteMask), .DataToMem(MemWriteData));
  partial_load partial_load_1 (
    .Instruction({funct7, nextInstruction[24:15], funct3, nextInstruction[11:0]}), .MemAddress(MemAddress),
    .DataFromMem(MemReadData), .DataToReg(DtoR));
  branch_comp branch_comp_1 (.BrData1(RRD1), .BrData2(RRD2), .BrUn(BrUn), .BrEq(BrEq), .BrLt(BrLt));
  imm_gen imm_gen_1 (
    .Instruction({funct7, nextInstruction[24:15], funct3, nextInstruction[11:0]}), .ImmSel(ImmSel),
    .Immediate(Imme));
  Priority_Encoder #(.select(2)) priority_encoder_1 (
    .in0(lb), .in1(lh), .in2(lw), .out(priority_encoder_1_out), .en_in(L));  // open: in3, gs, en_out
  Adder #(.width(6)) adder_3 (.a({4'b0000, priority_encoder_1_out}), .b(6'b001100), .out(L_Input));  // open: cin, cout

  // Other names for the same wires on the sheet: ALUR[31:0] = MemAddress; opcode[6:0] = nextInstruction[6:0];
  //   rd[4:0] = nextInstruction[11:7]; nextInstruction (some bits) = {funct7, funct3};
  //   rs1[4:0] = nextInstruction[19:15]; rs2[4:0] = nextInstruction[24:20]

  // Notes on the sheet:
  //   To IMEM
  //   IMEM (do **NOT** move this)
  //   From IMEM
  //   Inputs/Outputs for testing. Do **NOT** move these.
  //   It is OK to move the PC, RegFile, ALU, MEM, Branch Comp, Imm Gen, Partial Load, Partial Store and Control Logic to wherever is most convenient for you when constructing your CPU, and to delete this text
  //   To DMEM
  //   DMEM (do **NOT** move this)
  //   From DMEM
endmodule
