// Logisim project imm-gen.circ as structural Verilog: 1 circuit, main circuit imm_gen
module imm_gen (
  input  [31:0] Instruction,
  input  [2:0] ImmSel,
  output [31:0] Immediate
);

  wire [31:11] I_Immediate, S_Immediate;
  wire [31:12] B_Immediate;
  wire [31:20] J_Immediate;

  Multiplexer #(.enable("false"), .width(21)) multiplexer_1 (
    .in0({21{1'b0}}), .in1({21{1'b1}}), .out(I_Immediate), .sel(Instruction[31]));
  Multiplexer #(.enable("false"), .width(20)) multiplexer_2 (
    .in0({20{1'b0}}), .in1({20{1'b1}}), .out(B_Immediate), .sel(Instruction[31]));
  Multiplexer #(.enable("false"), .width(21)) multiplexer_3 (
    .in0({21{1'b0}}), .in1({21{1'b1}}), .out(S_Immediate), .sel(Instruction[31]));
  Multiplexer #(.enable("false"), .width(12)) multiplexer_4 (
    .in0({12{1'b0}}), .in1({12{1'b1}}), .out(J_Immediate), .sel(Instruction[31]));
  Multiplexer #(.enable("false"), .select(3), .width(32)) multiplexer_5 (
    .in0({I_Immediate, Instruction[30:20]}), .in1({S_Immediate, Instruction[30:25], Instruction[11:7]}),
    .in2({B_Immediate, Instruction[7], Instruction[30:25], Instruction[11:8], 1'b0}),
    .in3({Instruction[31:12], {12{1'b0}}}),
    .in4({J_Immediate, Instruction[19:12], Instruction[20], Instruction[30:21], 1'b0}), .out(Immediate),
    .sel(ImmSel));  // open: in5, in6, in7

  // Other names for the same wires on the sheet: I_Immediate[10:0] = Instruction[30:20];
  //   J_Immediate[19:1] = {Instruction[19:12], Instruction[20], Instruction[30:21]};
  //   U_Immediate[31:12] = Instruction[31:12];
  //   B_Immediate[11:1] = {Instruction[7], Instruction[30:25], Instruction[11:8]};
  //   S_Immediate[10:0] = {Instruction[30:25], Instruction[11:7]}

  // Notes on the sheet:
  //   INPUTS to your circuit
  //   DON'T CHANGE THE LOCATIONS OF THE INPUTS AND OUTPUTS!
  //   OUTPUT from your circuit
endmodule
