// Logisim project partial-load.circ as structural Verilog: 1 circuit, main circuit partial_load
module partial_load (
  input  [31:0] Instruction,
  input  [31:0] MemAddress,
  input  [31:0] DataFromMem,
  output [31:0] DataToReg
);

  wire comparator_2_eq, comparator_3_eq, comparator_4_eq, I_load, lb, lh, lw;
  wire [1:0] l_kind;
  wire [7:7] multiplexer_1_out;
  wire [15:15] multiplexer_2_out;
  wire [31:0] lbR, lhR;

  Comparator #(.mode("unsigned"), .width(7)) comparator_1 (
    .a(7'b0000011), .b(Instruction[6:0]), .eq(I_load));  // open: gt, lt
  Comparator #(.mode("unsigned"), .width(3)) comparator_2 (
    .a(3'b000), .b(Instruction[14:12]), .eq(comparator_2_eq));  // open: gt, lt
  Comparator #(.mode("unsigned"), .width(3)) comparator_3 (
    .a(3'b001), .b(Instruction[14:12]), .eq(comparator_3_eq));  // open: gt, lt
  Comparator #(.mode("unsigned"), .width(3)) comparator_4 (
    .a(3'b010), .b(Instruction[14:12]), .eq(comparator_4_eq));  // open: gt, lt
  Priority_Encoder #(.select(2)) priority_encoder_1 (
    .in0(lb), .in1(lh), .in2(lw), .out(l_kind));  // open: in3, gs, en_out, en_in
  and and_1 (lb, I_load, comparator_2_eq);
  and and_2 (lh, I_load, comparator_3_eq);
  and and_3 (lw, I_load, comparator_4_eq);
  Multiplexer #(.enable("false"), .select(2), .width(8)) multiplexer_1 (
    .in0(DataFromMem[7:0]), .in1(DataFromMem[15:8]), .in2(DataFromMem[23:16]), .in3(DataFromMem[31:24]),
    .out({multiplexer_1_out[7], lbR[6:0]}), .sel(MemAddress[1:0]));
  Multiplexer #(.enable("false"), .select(2), .width(16)) multiplexer_2 (
    .in0(DataFromMem[15:0]), .in1(DataFromMem[23:8]), .in2(DataFromMem[31:16]),
    .out({multiplexer_2_out[15], lhR[14:0]}), .sel(MemAddress[1:0]));  // open: in3
  Multiplexer #(.enable("false"), .width(25)) multiplexer_3 (
    .in0({25{1'b0}}), .in1({25{1'b1}}), .out(lbR[31:7]), .sel(multiplexer_1_out[7]));
  Multiplexer #(.enable("false"), .width(17)) multiplexer_4 (
    .in0({17{1'b0}}), .in1({17{1'b1}}), .out(lhR[31:15]), .sel(multiplexer_2_out[15]));
  Multiplexer #(.enable("false"), .select(2), .width(32)) multiplexer_5 (
    .in0(lbR), .in1(lhR), .in2(DataFromMem), .out(DataToReg), .sel(l_kind));  // open: in3

  // Other names for the same wires on the sheet: B0[7:0] = DataFromMem[7:0]; H0[15:0] = DataFromMem[15:0];
  //   B1[7:0] = DataFromMem[15:8]; H1[15:0] = DataFromMem[23:8]; B2[7:0] = DataFromMem[23:16];
  //   H2[15:0] = DataFromMem[31:16]; B3[7:0] = DataFromMem[31:24]; opcode[6:0] = Instruction[6:0];
  //   rd[4:0] = Instruction[11:7]; funct3[2:0] = Instruction[14:12]; rs1[4:0] = Instruction[19:15];
  //   imm[11:0] = Instruction[31:20]; MASel[1:0] = MemAddress[1:0]

  // Notes on the sheet:
  //   INPUTS to your circuit
  //   DON'T CHANGE THE LOCATIONS OF THE INPUTS AND OUTPUTS!
  //   OUTPUT from your circuit
endmodule
