// Logisim project partial-store.circ as structural Verilog: 1 circuit, main circuit partial_store
module partial_store (
  input  [31:0] Instruction,
  input  [31:0] MemAddress,
  input  [31:0] DataFromReg,
  input  MemWEn,
  output [3:0] MemWriteMask,
  output [31:0] DataToMem
);

  wire comparator_2_eq, comparator_3_eq, comparator_4_eq, S, sb, sh, sw;
  wire [1:0] s_kind;
  wire [3:0] multiplexer_3_out, sb_mwm, sh_mwm;
  wire [4:0] Shift_b;
  wire [31:0] sbR, shifter_1_out, shR;

  Comparator #(.mode("unsigned"), .width(7)) comparator_1 (
    .a(7'b0100011), .b(Instruction[6:0]), .eq(S));  // open: gt, lt
  Comparator #(.mode("unsigned"), .width(3)) comparator_2 (
    .a(3'b000), .b(Instruction[14:12]), .eq(comparator_2_eq));  // open: gt, lt
  Comparator #(.mode("unsigned"), .width(3)) comparator_3 (
    .a(3'b001), .b(Instruction[14:12]), .eq(comparator_3_eq));  // open: gt, lt
  Comparator #(.mode("unsigned"), .width(3)) comparator_4 (
    .a(3'b010), .b(Instruction[14:12]), .eq(comparator_4_eq));  // open: gt, lt
  Priority_Encoder #(.select(2)) priority_encoder_1 (
    .in0(sb), .in1(sh), .in2(sw), .out(s_kind));  // open: in3, gs, en_out, en_in
  and and_1 (sb, S, comparator_2_eq);
  and and_2 (sh, S, comparator_3_eq);
  and and_3 (sw, S, comparator_4_eq);
  Shifter #(.width(32)) shifter_1 (.in({{16{1'b0}}, DataFromReg[15:0]}), .\dist (5'b10000), .out(shifter_1_out));
  Shifter #(.width(32)) shifter_2 (.in({{24{1'b0}}, DataFromReg[7:0]}), .\dist (Shift_b), .out(sbR));
  Multiplexer #(.enable("false"), .select(2), .width(32)) multiplexer_1 (
    .in0({{16{1'b0}}, DataFromReg[15:0]}), .in2(shifter_1_out), .out(shR), .sel(MemAddress[1:0]));  // open: in1, in3
  Multiplexer #(.enable("false"), .select(2), .width(32)) multiplexer_2 (
    .in0(sbR), .in1(shR), .in2(DataFromReg), .out(DataToMem), .sel(s_kind));  // open: in3
  Shifter #(.width(5)) shifter_3 (.in({3'b000, MemAddress[1:0]}), .\dist (3'b011), .out(Shift_b));
  Shifter #(.width(4)) shifter_4 (.in(4'b0001), .\dist (MemAddress[1:0]), .out(sb_mwm));
  Shifter #(.width(4)) shifter_5 (.in(4'b0011), .\dist (MemAddress[1:0]), .out(sh_mwm));
  Multiplexer #(.enable("false"), .select(2), .width(4)) multiplexer_3 (
    .in0(sb_mwm), .in1(sh_mwm), .in2(4'b1111), .out(multiplexer_3_out), .sel(s_kind));  // open: in3
  Multiplexer #(.enable("false"), .width(4)) multiplexer_4 (
    .in0(4'b0000), .in1(multiplexer_3_out), .out(MemWriteMask), .sel(MemWEn));

  // Other names for the same wires on the sheet: MASel[1:0] = MemAddress[1:0]; d0_7[7:0] = DataFromReg[7:0];
  //   d0_15[15:0] = DataFromReg[15:0]; opcode[6:0] = Instruction[6:0]; funct3[2:0] = Instruction[14:12];
  //   funct7[6:0] = Instruction[31:25]

  // Notes on the sheet:
  //   INPUTS to your circuit
  //   DON'T CHANGE THE LOCATIONS OF THE INPUTS AND OUTPUTS!
  //   OUTPUT from your circuit
endmodule
