// Logisim project regfile.circ as structural Verilog: 1 circuit, main circuit regfile
module regfile (
  input  [4:0] ReadReg1,
  input  [4:0] ReadReg2,
  input  [4:0] WriteReg,
  input  [31:0] RegWriteData,
  input  RegWEn,
  input  clk,
  output [31:0] ra,
  output [31:0] sp,
  output [31:0] t0,
  output [31:0] t1,
  output [31:0] t2,
  output [31:0] s0,
  output [31:0] s1,
  output [31:0] a0,
  output [31:0] RegReadData1,
  output [31:0] RegReadData2
);

  wire c0, c1, c2, c3, c4, c5, c6, c7, c8, c9, c10, c11, c12, c13, c14, c15, c16, c17, c18, c19, c20, c21,
       c22, c23, c24, c25, c26, c27, c28, c29, c30, c31;
  wire [31:0] RegOutput0, RegOutput3, RegOutput4, RegOutput11, RegOutput12, RegOutput13, RegOutput14,
       RegOutput15, RegOutput16, RegOutput17, RegOutput18, RegOutput19, RegOutput20, RegOutput21,
       RegOutput22, RegOutput23, RegOutput24, RegOutput25, RegOutput26, RegOutput27, RegOutput28,
       RegOutput29, RegOutput30, RegOutput31;

  Register #(.width(32)) x0 (.D(RegWriteData), .en(c0), .clk(clk), .Q(RegOutput0), .clr(1'b1));
  Register #(.width(32)) x1 (.D(RegWriteData), .en(c1), .clk(clk), .Q(ra));  // open: clr
  Register #(.width(32)) x2 (.D(RegWriteData), .en(c2), .clk(clk), .Q(sp));  // open: clr
  Register #(.width(32)) x5 (.D(RegWriteData), .en(c5), .clk(clk), .Q(t0));  // open: clr
  Register #(.width(32)) x8 (.D(RegWriteData), .en(c8), .clk(clk), .Q(s0));  // open: clr
  Register #(.width(32)) x11 (.D(RegWriteData), .en(c11), .clk(clk), .Q(RegOutput11));  // open: clr
  Register #(.width(32)) x14 (.D(RegWriteData), .en(c14), .clk(clk), .Q(RegOutput14));  // open: clr
  Register #(.width(32)) x17 (.D(RegWriteData), .en(c17), .clk(clk), .Q(RegOutput17));  // open: clr
  Register #(.width(32)) x20 (.D(RegWriteData), .en(c20), .clk(clk), .Q(RegOutput20));  // open: clr
  Register #(.width(32)) x23 (.D(RegWriteData), .en(c23), .clk(clk), .Q(RegOutput23));  // open: clr
  Register #(.width(32)) x26 (.D(RegWriteData), .en(c26), .clk(clk), .Q(RegOutput26));  // open: clr
  Register #(.width(32)) x29 (.D(RegWriteData), .en(c29), .clk(clk), .Q(RegOutput29));  // open: clr
  Multiplexer #(.enable("false"), .select(5), .width(32)) multiplexer_1 (
    .in0(RegOutput0), .in1(ra), .in2(sp), .in3(RegOutput3), .in4(RegOutput4), .in5(t0), .in6(t1), .in7(t2),
    .in8(s0), .in9(s1), .in10(a0), .in11(RegOutput11), .in12(RegOutput12), .in13(RegOutput13),
    .in14(RegOutput14), .in15(RegOutput15), .in16(RegOutput16), .in17(RegOutput17), .in18(RegOutput18),
    .in19(RegOutput19), .in20(RegOutput20), .in21(RegOutput21), .in22(RegOutput22), .in23(RegOutput23),
    .in24(RegOutput24), .in25(RegOutput25), .in26(RegOutput26), .in27(RegOutput27), .in28(RegOutput28),
    .in29(RegOutput29), .in30(RegOutput30), .in31(RegOutput31), .out(RegReadData1), .sel(ReadReg1));
  Register #(.width(32)) x3 (.D(RegWriteData), .en(c3), .clk(clk), .Q(RegOutput3));  // open: clr
  Register #(.width(32)) x6 (.D(RegWriteData), .en(c6), .clk(clk), .Q(t1));  // open: clr
  Register #(.width(32)) x9 (.D(RegWriteData), .en(c9), .clk(clk), .Q(s1));  // open: clr
  Register #(.width(32)) x12 (.D(RegWriteData), .en(c12), .clk(clk), .Q(RegOutput12));  // open: clr
  Register #(.width(32)) x15 (.D(RegWriteData), .en(c15), .clk(clk), .Q(RegOutput15));  // open: clr
  Register #(.width(32)) x18 (.D(RegWriteData), .en(c18), .clk(clk), .Q(RegOutput18));  // open: clr
  Register #(.width(32)) x21 (.D(RegWriteData), .en(c21), .clk(clk), .Q(RegOutput21));  // open: clr
  Register #(.width(32)) x24 (.D(RegWriteData), .en(c24), .clk(clk), .Q(RegOutput24));  // open: clr
  Register #(.width(32)) x27 (.D(RegWriteData), .en(c27), .clk(clk), .Q(RegOutput27));  // open: clr
  Register #(.width(32)) x30 (.D(RegWriteData), .en(c30), .clk(clk), .Q(RegOutput30));  // open: clr
  Register #(.width(32)) x4 (.D(RegWriteData), .en(c4), .clk(clk), .Q(RegOutput4));  // open: clr
  Register #(.width(32)) x7 (.D(RegWriteData), .en(c7), .clk(clk), .Q(t2));  // open: clr
  Register #(.width(32)) x10 (.D(RegWriteData), .en(c10), .clk(clk), .Q(a0));  // open: clr
  Register #(.width(32)) x13 (.D(RegWriteData), .en(c13), .clk(clk), .Q(RegOutput13));  // open: clr
  Register #(.width(32)) x16 (.D(RegWriteData), .en(c16), .clk(clk), .Q(RegOutput16));  // open: clr
  Register #(.width(32)) x19 (.D(RegWriteData), .en(c19), .clk(clk), .Q(RegOutput19));  // open: clr
  Register #(.width(32)) x22 (.D(RegWriteData), .en(c22), .clk(clk), .Q(RegOutput22));  // open: clr
  Register #(.width(32)) x25 (.D(RegWriteData), .en(c25), .clk(clk), .Q(RegOutput25));  // open: clr
  Register #(.width(32)) x28 (.D(RegWriteData), .en(c28), .clk(clk), .Q(RegOutput28));  // open: clr
  Register #(.width(32)) x31 (.D(RegWriteData), .en(c31), .clk(clk), .Q(RegOutput31));  // open: clr
  Multiplexer #(.enable("false"), .select(5), .width(32)) multiplexer_2 (
    .in0(RegOutput0), .in1(ra), .in2(sp), .in3(RegOutput3), .in4(RegOutput4), .in5(t0), .in6(t1), .in7(t2),
    .in8(s0), .in9(s1), .in10(a0), .in11(RegOutput11), .in12(RegOutput12), .in13(RegOutput13),
    .in14(RegOutput14), .in15(RegOutput15), .in16(RegOutput16), .in17(RegOutput17), .in18(RegOutput18),
    .in19(RegOutput19), .in20(RegOutput20), .in21(RegOutput21), .in22(RegOutput22), .in23(RegOutput23),
    .in24(RegOutput24), .in25(RegOutput25), .in26(RegOutput26), .in27(RegOutput27), .in28(RegOutput28),
    .in29(RegOutput29), .in30(RegOutput30), .in31(RegOutput31), .out(RegReadData2), .sel(ReadReg2));
  Decoder #(.select(5)) decoder_1 (
    .out0(c0), .out1(c1), .out2(c2), .out3(c3), .out4(c4), .out5(c5), .out6(c6), .out7(c7), .out8(c8),
    .out9(c9), .out10(c10), .out11(c11), .out12(c12), .out13(c13), .out14(c14), .out15(c15), .out16(c16),
    .out17(c17), .out18(c18), .out19(c19), .out20(c20), .out21(c21), .out22(c22), .out23(c23), .out24(c24),
    .out25(c25), .out26(c26), .out27(c27), .out28(c28), .out29(c29), .out30(c30), .out31(c31),
    .sel(WriteReg), .en(RegWEn));

  // Other names for the same wires on the sheet: RegOutput1[31:0] = ra; RegOutput2[31:0] = sp; RegOutput5[31:0] = t0;
  //   RegOutput6[31:0] = t1; RegOutput7[31:0] = t2; RegOutput8[31:0] = s0; RegOutput9[31:0] = s1;
  //   RegOutput10[31:0] = a0

  // Notes on the sheet:
  //   INPUTS to your circuit
  //   DON'T CHANGE THE LOCATIONS OF THE INPUTS AND OUTPUTS!
  //   These are DEBUG/TEST outputs from your circuit.
  //   OUTPUTS from your circuit
endmodule
